# Fritzing sketch Wiring Diagram (saved by Fritzing 0.9.3b)

parts:
  8_Channel_Relay1 = 8 Channel Power Relay
  U1 = ESP8266 NodeMCU LoLin module

nets:
  GND: 8_Channel_Relay1.GND, U1.GND
  N1: 8_Channel_Relay1.IN1, U1.D1
  N2: 8_Channel_Relay1.IN2, U1.D2
  N3: 8_Channel_Relay1.IN3, U1.D5
  N4: 8_Channel_Relay1.IN4, U1.D6
  N5: 8_Channel_Relay1.IN5, U1.D7
  VCC: 8_Channel_Relay1.VCC, U1.Vin

custom parts:
  8 Channel Power Relay: An 8 channel power relay. The module operates at 5V.
  ESP8266 NodeMCU LoLin module: ESP8266 based NodeMCU
